// Logisim project 1 TO 4 DE-MUX.circ as structural Verilog: 1 circuit, main circuit main
module main (
  input  S0,
  input  S1,
  input  I,
  output Y0_S0_prime_S1_prime_I,
  output Y1_S0_prime_S1I,
  output Y2_S0S1_prime_I,
  output Y3_S0S1I
);

  wire not_1_out, not_2_out;

  not not_1 (not_1_out, S0);
  not not_2 (not_2_out, S1);
  and and_1 (Y0_S0_prime_S1_prime_I, not_1_out, not_2_out, I);
  and and_2 (Y1_S0_prime_S1I, not_1_out, S1, I);
  and and_3 (Y2_S0S1_prime_I, S0, not_2_out, I);
  and and_4 (Y3_S0S1I, S0, S1, I);

  // Notes on the sheet:
  //   S0'
  //   S1'
  //   1 TO 4 DE-MULTIPLEXER
endmodule
