// Logisim project 1 TO 8 DE-MUX.circ as structural Verilog: 1 circuit, main circuit main
module main (
  input  S0,
  input  S1,
  input  S2,
  input  I,
  output Y0,
  output Y1,
  output Y2,
  output Y3,
  output Y4,
  output Y5,
  output Y6,
  output Y7
);

  wire not_1_out, not_2_out, not_3_out;

  not not_1 (not_1_out, S0);
  not not_2 (not_2_out, S1);
  not not_3 (not_3_out, S2);
  and and_1 (Y0, not_1_out, not_2_out, not_3_out, I);
  and and_2 (Y1, not_1_out, not_2_out, S2, I);
  and and_3 (Y2, not_1_out, S1, not_3_out, I);
  and and_4 (Y3, not_1_out, S1, S2, I);
  and and_5 (Y4, S0, not_2_out, not_3_out, I);
  and and_6 (Y5, S0, not_2_out, S2, I);
  and and_7 (Y6, S0, S1, not_3_out, I);
  and and_8 (Y7, S0, S1, S2, I);

  // Notes on the sheet:
  //   S0'
  //   S1'
  //   S2'
  //   S0'S1'S2'I
  //   S0'S1'S2I
  //   S0'S1S2'I
  //   S0'S1S2I
  //   S0S1'S2'I
  //   S0S1'S2I
  //   S0S1S2'I
  //   S0S1S2I
  //   8 TO 1 DE-MUX
endmodule
