// Logisim project 2 TO 4 DECODER.circ as structural Verilog: 1 circuit, main circuit main
module main (
  input  A,
  input  B,
  input  A_2,
  input  B_2,
  input  C,
  output D0,
  output Q0,
  output D1,
  output Q1,
  output D2,
  output Q2,
  output D3,
  output Q3,
  output D4,
  output D5,
  output D6,
  output D7
);

  wire not_1_out, not_2_out, not_3_out, not_4_out, not_5_out;

  not not_1 (not_1_out, A);
  not not_2 (not_2_out, B);
  and and_1 (Q0, not_1_out, not_2_out);
  and and_2 (Q1, not_1_out, B);
  and and_3 (Q2, A, not_2_out);
  and and_4 (Q3, A, B);
  not not_3 (not_3_out, A_2);
  not not_4 (not_4_out, B_2);
  not not_5 (not_5_out, C);
  and and_5 (D0, not_3_out, not_4_out, not_5_out);
  and and_6 (D1, not_3_out, not_4_out, C);
  and and_7 (D2, not_3_out, B_2, not_5_out);
  and and_8 (D3, not_3_out, B_2, C);
  and and_9 (D4, A_2, not_4_out, not_5_out);
  and and_10 (D5, A_2, not_4_out, C);
  and and_11 (D6, A_2, B_2, not_5_out);
  and and_12 (D7, A_2, B_2, C);

  // Notes on the sheet:
  //   A'
  //   B'
  //   A'
  //   B'
  //   A'
  //   B
  //   A
  //   B'
  //   A
  //   B
  //   2 TO 4 DECODER
  //   A'B'
  //   A'B
  //   AB'
  //   AB
  //   A'
  //   B'
  //   C'
endmodule
