// Logisim project 4 TO 1 MULTIPLEXER.circ as structural Verilog: 1 circuit, main circuit main
module main (
  input  S0,
  input  S1,
  input  I0,
  input  I1,
  input  I2,
  input  I3,
  output out_7
);

  wire and_1_out, and_2_out, and_3_out, and_4_out, not_1_out, not_2_out;

  not not_1 (not_1_out, S0);
  not not_2 (not_2_out, S1);
  and and_1 (and_1_out, not_1_out, not_2_out, I0);
  and and_2 (and_2_out, not_1_out, S1, I1);
  and and_3 (and_3_out, S0, not_2_out, I2);
  and and_4 (and_4_out, S0, S1, I3);
  or or_1 (out_7, and_1_out, and_2_out, and_3_out, and_4_out);

  // Notes on the sheet:
  //   S0'
  //   S1'
  //   S0'S1'I0
  //   S0'S1I1
  //   S0S1'I2
  //   S0S1I3
  //   4 TO 1 MULTIPLEXER
  //   Y = S0'S1'I0 + S0'S1I1 + S0S1'I2 + S0S1I3 
endmodule
