// Logisim project 4 to 1 mul using nand.circ as structural Verilog: 1 circuit, main circuit main
module main (
  input  S0,
  input  S1,
  input  I0,
  input  I1,
  input  I2,
  input  I3,
  input  S0_2,
  input  S1_2,
  input  I0_2,
  input  I1_2,
  input  I2_2,
  input  I3_2,
  output Y,
  output Y_2
);

  wire nand_1_out, nand_2_out, nand_3_out, nand_4_out, nand_5_out, nand_6_out, nand_7_out, nand_8_out,
       nand_9_out, nand_10_out, nand_11_out, nand_12_out;

  nand nand_1 (nand_1_out, S0_2, S0_2);
  nand nand_2 (nand_2_out, S0, S0);
  nand nand_3 (nand_3_out, S1_2, S1_2);
  nand nand_4 (nand_4_out, S1, S1);
  nand nand_5 (nand_5_out, nand_1_out, I0_2, nand_3_out);
  nand nand_6 (nand_6_out, S0_2, I1_2, S1_2);
  nand nand_7 (nand_7_out, nand_1_out, I2_2, nand_3_out);
  nand nand_8 (nand_8_out, S0_2, I3_2, S1_2);
  nand nand_9 (nand_9_out, nand_2_out, nand_4_out, I0);
  nand nand_10 (nand_10_out, nand_2_out, S1, I1);
  nand nand_11 (nand_11_out, S0, nand_4_out, I2);
  nand nand_12 (nand_12_out, S0, S1, I3);
  nand nand_13 (Y_2, nand_5_out, nand_6_out, nand_7_out, nand_8_out);
  nand nand_14 (Y, nand_9_out, nand_10_out, nand_11_out, nand_12_out);

  // Notes on the sheet:
  //   S0'
  //   S0'
  //   S1'
  //   S1'
  //   4 TO 1 MULTIPLEXER
  //   S0S1I3
  //   S0'S1I1
  //   S0S1'I2
  //   S0S1I3
  //   S0'S1'I0
  //   S0'S1I1
  //   S0S1'I2
  //   S0'S1'I0
  //   4 TO 1 MULTIPLEXER
  //   Y = S0'S1'I0 + S0'S1I1 + S0S1'I2 + S0S1I3 
  //   Y = S0'S1'I0 + S0'S1I1 + S0S1'I2 + S0S1I3 
endmodule
