// Logisim project 8 to 1 multiplexer.circ as structural Verilog: 1 circuit, main circuit main
module main (
  input  S0,
  input  S1,
  input  S2,
  input  I0,
  input  I1,
  input  I2,
  input  I3,
  input  I4,
  input  I5,
  input  I6,
  input  I7,
  output Y
);

  wire and_1_out, and_2_out, and_3_out, and_4_out, and_5_out, and_6_out, and_7_out, and_8_out, not_1_out,
       not_2_out, not_3_out;

  not not_1 (not_1_out, S0);
  not not_2 (not_2_out, S1);
  not not_3 (not_3_out, S2);
  and and_1 (and_1_out, not_1_out, not_2_out, not_3_out, I0);
  and and_2 (and_2_out, not_1_out, not_2_out, S2, I1);
  and and_3 (and_3_out, not_1_out, S1, not_3_out, I2);
  and and_4 (and_4_out, not_1_out, S1, S2, I3);
  and and_5 (and_5_out, S0, not_2_out, not_3_out, I4);
  and and_6 (and_6_out, S0, not_2_out, S2, I5);
  and and_7 (and_7_out, S0, S1, not_3_out, I6);
  and and_8 (and_8_out, S0, S1, S2, I7);
  or or_1 (Y, and_1_out, and_2_out, and_3_out, and_4_out, and_5_out, and_6_out, and_7_out, and_8_out);

  // Notes on the sheet:
  //   8 TO 1 MULTIPLEXER
  //   S0'
  //   S1'
  //   S2'
  //   S0'S1'S2'I0
  //   S0'S1'S2I1
  //   S0'S1S2'I2
  //   S0'S1S2I3
  //   S0S1'S2'I4
  //   S0S1'S2I5
  //   S0S1S2'I6
  //   S0S1S2I7
endmodule
