// Logisim project ADDER.circ as structural Verilog: 1 circuit, main circuit main
module main (
  input  A,
  input  B,
  input  Cin,
  output CARRY,
  output SUM
);

  wire and_1_out, and_2_out, xor_1_out;

  xor xor_1 (xor_1_out, A, B);
  and and_1 (and_1_out, A, B);
  xor xor_2 (SUM, xor_1_out, Cin);
  and and_2 (and_2_out, xor_1_out, Cin);
  or or_1 (CARRY, and_1_out, and_2_out);

  // Notes on the sheet:
  //   FULL ADDER
  //   A
  //   B
  //   A XOR B
  //   Cin
  //   A XOR B
  //   Cin
  //   A.B
  //   A XOR B XOR Cin
  //   (A XOR B).Cin
  //   (A.B) + (A XOR B).Cin
endmodule
