// Logisim project BCD TO EX-3.circ as structural Verilog: 1 circuit, main circuit main
module main (
  input  A,
  input  B,
  input  C,
  input  D,
  output W___A_BC_BD,
  output Y___CD__C_prime_D_prime,
  output Z__D_prime,
  output out_8
);

  wire and_1_out, and_2_out, and_3_out, and_4_out, and_5_out, and_6_out, and_7_out, not_1_out, not_2_out,
       not_3_out, not_4_out, not_5_out, not_6_out;

  not not_1 (not_1_out, C);
  not not_2 (not_2_out, D);
  not not_3 (not_3_out, B);
  not not_4 (not_4_out, B);
  not not_5 (not_5_out, C);
  not not_6 (not_6_out, D);
  and and_1 (and_1_out, B, C);
  and and_2 (and_2_out, B, D);
  and and_3 (and_3_out, C, D);
  and and_4 (and_4_out, not_1_out, not_2_out);
  not not_7 (Z__D_prime, D);
  and and_5 (and_5_out, not_3_out, C);
  and and_6 (and_6_out, not_4_out, D);
  and and_7 (and_7_out, B, not_5_out, not_6_out);
  or or_1 (W___A_BC_BD, A, and_1_out, and_2_out);
  or or_2 (Y___CD__C_prime_D_prime, and_3_out, and_4_out);
  or or_3 (out_8, and_5_out, and_6_out, and_7_out);

  // Notes on the sheet:
  //   BCD TO EXCESS-3
  //   X = B'C + B'D + BC'D'
endmodule
