// Logisim project D FLIP FLOP.circ as structural Verilog: 1 circuit, main circuit main
module main (
  input  Clk,
  input  S,
  input  Clk_2,
  input  S_2,
  output Q_t,
  output Q_t__prime,
  output Q_t_2,
  output Q_t__prime_2
);

  wire and_1_out, and_2_out, nand_1_out, nand_2_out, nand_3_out, not_1_out;

  not not_1 (not_1_out, S);
  nand nand_1 (nand_1_out, S_2, S_2);
  and and_1 (and_1_out, not_1_out, Clk);
  and and_2 (and_2_out, Clk, S);
  nand nand_2 (nand_2_out, nand_1_out, Clk_2);
  nand nand_3 (nand_3_out, Clk_2, S_2);
  nor nor_1 (Q_t, and_1_out, Q_t__prime);
  nor nor_2 (Q_t__prime, Q_t, and_2_out);
  nand nand_4 (Q_t_2, nand_2_out, Q_t__prime_2);
  nand nand_5 (Q_t__prime_2, Q_t_2, nand_3_out);

  // Notes on the sheet:
  //   D Flip-Flop
  //   D Flip-Flop using NAND
endmodule
