// Logisim project D Latch.circ as structural Verilog: 1 circuit, main circuit main
module main (
  input  D,
  input  E,
  input  D_2,
  input  E_2,
  output Q_t,
  output Q_t__prime,
  output Q_t_2,
  output Q_t__prime_2
);

  wire and_1_out, and_2_out, nand_1_out, nand_2_out, not_1_out, not_2_out;

  not not_1 (not_1_out, D);
  not not_2 (not_2_out, D_2);
  nand nand_1 (nand_1_out, D, E);
  nand nand_2 (nand_2_out, E, not_1_out);
  and and_1 (and_1_out, D_2, E_2);
  and and_2 (and_2_out, E_2, not_2_out);
  nand nand_3 (Q_t, nand_1_out, Q_t__prime);
  nand nand_4 (Q_t__prime, Q_t, nand_2_out);
  nor nor_1 (Q_t_2, and_1_out, Q_t__prime_2);
  nor nor_2 (Q_t__prime_2, Q_t_2, and_2_out);

  // Notes on the sheet:
  //   D LATCH
  //   D LATCH
endmodule
