// Logisim project DE-MUX USING NAND GATE.circ as structural Verilog: 1 circuit, main circuit main
module main (
  input  in_1,
  input  in_2,
  input  I,
  input  S0,
  input  S1,
  output I0,
  output I1,
  output Y0_S0_prime_S1_prime_I,
  output Y1_S0_prime_S1I,
  output Y2_S0S1_prime_I,
  output Y3_S0S1I
);

  wire nand_1_out, nand_2_out, nand_3_out, nand_4_out, nand_5_out, nand_6_out, nand_7_out, nand_8_out;

  nand nand_1 (nand_1_out, S0, S0);
  nand nand_2 (nand_2_out, in_2, in_2);
  nand nand_3 (nand_3_out, S1, S1);
  nand nand_4 (nand_4_out, in_1, nand_2_out);
  nand nand_5 (nand_5_out, nand_1_out, I, nand_3_out);
  nand nand_6 (nand_6_out, S0, I, S1);
  nand nand_7 (nand_7_out, nand_1_out, I, nand_3_out);
  nand nand_8 (nand_8_out, S0, I, S1);
  nand nand_9 (I0, nand_4_out, nand_4_out);
  nand nand_10 (I1, in_1, in_2);
  nand nand_11 (Y0_S0_prime_S1_prime_I, nand_5_out, nand_5_out);
  nand nand_12 (Y1_S0_prime_S1I, nand_6_out, nand_6_out);
  nand nand_13 (Y2_S0S1_prime_I, nand_7_out, nand_7_out);
  nand nand_14 (Y3_S0S1I, nand_8_out, nand_8_out);

  // Notes on the sheet:
  //   4 TO 1 DE-MULTIPLEXER
  //   S0'
  //   S1'
  //   1 X 2 DE-MULTIPLEXER
  //   (S0'S1'I)'
  //   (S0'S1I)'
  //   (S0S1'I)'
  //   (S0S1I)'
endmodule
