// Logisim project ENCODER.circ as structural Verilog: 1 circuit, main circuit main
module main (
  input  Y3,
  input  Y2,
  input  Y1,
  input  Y1_2,
  input  Y2_2,
  input  Y3_2,
  input  Y4,
  input  Y5,
  input  Y6,
  input  Y7,
  output A0_Y3_Y2,
  output A1_Y3_Y1,
  output A2___Y4_Y5_Y6_Y7,
  output out_14,
  output out_15
);

  or or_1 (A2___Y4_Y5_Y6_Y7, Y7, Y6, Y5, Y4);
  or or_2 (A0_Y3_Y2, Y3, Y2);
  or or_3 (A1_Y3_Y1, Y3, Y1);
  or or_4 (out_14, Y7, Y6, Y3_2, Y2_2);
  or or_5 (out_15, Y7, Y5, Y3_2, Y1_2);

  // Notes on the sheet:
  //   4 TO 2 ENCODER
  //   8 TO 3 ENCODER
  //   A1=Y2+Y3+Y6+Y7
  //   A0=Y1+Y3+Y5+Y7
endmodule
