// Logisim project EX-3 TO BCD.circ as structural Verilog: 1 circuit, main circuit main
module main (
  input  A,
  input  B,
  input  C,
  input  D,
  output W_AB_ACD,
  output out_6,
  output Y_C_prime_D_CD_prime,
  output Z_D_prime
);

  wire and_1_out, and_2_out, and_3_out, and_4_out, and_5_out, and_6_out, and_7_out, not_1_out, not_2_out,
       not_3_out, not_4_out, not_5_out, not_6_out;

  not not_1 (not_1_out, B);
  not not_2 (not_2_out, C);
  not not_3 (not_3_out, B);
  not not_4 (not_4_out, D);
  not not_5 (not_5_out, C);
  not not_6 (not_6_out, D);
  not not_7 (Z_D_prime, D);
  and and_1 (and_1_out, A, B);
  and and_2 (and_2_out, A, C, D);
  and and_3 (and_3_out, not_1_out, not_2_out);
  and and_4 (and_4_out, not_3_out, not_4_out);
  and and_5 (and_5_out, B, C, D);
  and and_6 (and_6_out, not_5_out, D);
  and and_7 (and_7_out, C, not_6_out);
  or or_1 (W_AB_ACD, and_1_out, and_2_out);
  or or_2 (out_6, and_3_out, and_4_out, and_5_out);
  or or_3 (Y_C_prime_D_CD_prime, and_6_out, and_7_out);

  // Notes on the sheet:
  //   AB
  //   ACD
  //   B'C'
  //   B'D'
  //   BCD
  //   C'D
  //   CD'
  //   D'
  //   EXCESS-3 TO BCD
  //   X = B'C'+B'D'+BCD
endmodule
