// Logisim project HALF ADDER USING NOR.circ as structural Verilog: 1 circuit, main circuit main
module main (
  input  A,
  input  B,
  output AB,
  output SUM
);

  wire nor_1_out, nor_2_out, nor_3_out;

  nor nor_1 (nor_1_out, A, B);
  nor nor_2 (nor_2_out, A, A);
  nor nor_3 (nor_3_out, B, B);
  nor nor_4 (AB, nor_2_out, nor_3_out);
  nor nor_5 (SUM, AB, nor_1_out);

  // Notes on the sheet:
  //   HALF ADDER USING NOR GATE
  //   (A+B)'
  //   A
  //   B
  //   B'
  //   A'
  //   (A+B)'
  //   AB
  //   CARRY
  //   (A'B+AB')
endmodule
