// Logisim project HALF SUBS USING NOR.circ as structural Verilog: 1 circuit, main circuit main
module main (
  input  A,
  input  B,
  output out_3,
  output DIFFERENCE
);

  wire nor_1_out, nor_3_out, nor_4_out;

  nor nor_1 (nor_1_out, A, B);
  nor nor_2 (out_3, A, nor_1_out);
  nor nor_3 (nor_3_out, nor_1_out, B);
  nor nor_4 (nor_4_out, out_3, nor_3_out);
  nor nor_5 (DIFFERENCE, nor_4_out, nor_4_out);

  // Notes on the sheet:
  //   HALF SUBSTRACTOR USING NOR GATE
  //   (A+B)'
  //   A
  //   (A+B)'
  //   B
  //   ((A+B)'+B)'
  //   (A+(A+B)')'
  //   BORROW
  //   (A'B+AB')
endmodule
