// Logisim project JK FLIP-FLOP.circ as structural Verilog: 1 circuit, main circuit main
module main (
  input  J,
  input  in_2,
  input  in_3,
  input  Clk,
  input  in_5,
  input  K,
  input  k_2,
  input  Clk_2,
  input  j_2,
  output Q_t,
  output out_11,
  output out_12,
  output Q_t__prime,
  output Q,
  output Q_prime
);

  wire and_1_out, and_2_out, and_3_out, and_4_out, nand_1_out, nand_2_out;

  and and_1 (and_1_out, Q_t, J, Clk);
  and and_2 (and_2_out, Clk, K, Q_t__prime);
  nand nand_1 (nand_1_out, Q, k_2, Clk_2);
  nand nand_2 (nand_2_out, Clk_2, j_2, Q_prime);
  nor nor_1 (Q_t, and_1_out, Q_t__prime);
  nor nor_2 (Q_t__prime, Q_t, and_2_out);
  nand nand_3 (Q, nand_1_out, Q_prime);
  nand nand_4 (Q_prime, Q, nand_2_out);
  and and_3 (and_3_out, out_11, in_2, in_3);
  and and_4 (and_4_out, in_3, in_5, out_12);
  nor nor_3 (out_11, and_3_out, out_12);
  nor nor_4 (out_12, out_11, and_4_out);

  // Notes on the sheet:
  //   JK Flip-Flop
  //   JK Flip-Flop using NAND gate
endmodule
