// Logisim project LAB 1.circ as structural Verilog: 1 circuit, main circuit main
module main (
  input  A,
  input  B,
  input  C,
  input  A_2,
  input  A_3,
  input  B_2,
  input  B_3,
  input  C_2,
  input  A_4,
  input  B_4,
  input  C_3,
  output A_B_prime_C_prime,
  output AC_BC,
  output A_B___A_B__prime,
  output A_B_C__A_B_prime_C_prime
);

  wire and_1_out, and_2_out, and_3_out, nand_1_out, nand_2_out, nor_1_out, not_1_out, not_2_out, not_3_out,
       not_4_out, or_1_out, or_4_out;

  not not_1 (not_1_out, B_4);
  not not_2 (not_2_out, C_3);
  and and_1 (and_1_out, A_3, B_3);
  nor nor_1 (nor_1_out, A_3, B_3);
  or or_1 (or_1_out, not_1_out, not_2_out);
  and and_2 (and_2_out, A_4, B_4, C_3);
  and and_3 (and_3_out, or_1_out, A_4);
  or or_2 (A_B___A_B__prime, and_1_out, nor_1_out);
  or or_3 (A_B_C__A_B_prime_C_prime, and_2_out, and_3_out);
  not not_3 (not_3_out, B);
  not not_4 (not_4_out, C);
  or or_4 (or_4_out, not_3_out, not_4_out);
  and and_4 (A_B_prime_C_prime, A, or_4_out);
  nand nand_1 (nand_1_out, A_2, B_2);
  nand nand_2 (nand_2_out, B_2, C_2);
  nand nand_3 (AC_BC, nand_1_out, nand_2_out);

  // Notes on the sheet:
  //   03/02/2021
  //   Q = (A.B) + (A+B)'
  //   Q = (A.B.C) + A(B'+C')
  //   LAB ASSIGNMENT 1
  //   A
  //   B
  //   A
  //   B
  //   A.B
  //   (B'+C')
  //   A
  //   (A+B)'
  //   A.B.C
  //   A
  //   (B'+C')
  //   (A.B)'
  //   (B.C)'
endmodule
