// Logisim project MASTER SLAVE JK FLIP FLOP USING NAND.circ as structural Verilog: 1 circuit, main circuit main
module main (
  input  K,
  input  Clk,
  input  J,
  output Q_t,
  output Q_t__prime
);

  wire nand_1_out, nand_2_out, nand_3_out, nand_4_out, nand_5_out, nand_6_out, not_1_out;

  nand nand_1 (nand_1_out, nand_3_out, K, Clk);
  nand nand_2 (nand_2_out, Clk, J, nand_4_out);
  not not_1 (not_1_out, Clk);
  nand nand_3 (nand_3_out, nand_1_out, nand_4_out);
  nand nand_4 (nand_4_out, nand_3_out, nand_2_out);
  nand nand_5 (nand_5_out, nand_3_out, Q_t, not_1_out);
  nand nand_6 (nand_6_out, not_1_out, Q_t__prime, nand_4_out);
  nand nand_7 (Q_t, nand_5_out, Q_t__prime);
  nand nand_8 (Q_t__prime, Q_t, nand_6_out);

  // Notes on the sheet:
  //   MASTER SLAVE JK FLIP FLOP
endmodule
