// Logisim project SR LATCH.circ as structural Verilog: 1 circuit, main circuit main
module main (
  input  S,
  input  E,
  input  R,
  input  S_2,
  input  R_2,
  output Q_t,
  output Q_t__prime,
  output Q_t_2,
  output Q_t__prime_2
);

  wire and_1_out, and_2_out;

  and and_1 (and_1_out, S, E);
  and and_2 (and_2_out, E, R);
  nand nand_1 (Q_t_2, S_2, Q_t__prime_2);
  nand nand_2 (Q_t__prime_2, Q_t_2, R_2);
  nor nor_1 (Q_t, and_1_out, Q_t__prime);
  nor nor_2 (Q_t__prime, Q_t, and_2_out);

  // Notes on the sheet:
  //   SR Latch
endmodule
