// Logisim project SUBTRACTOR.circ as structural Verilog: 1 circuit, main circuit main
module main (
  input  A,
  input  B,
  input  A_2,
  input  B_2,
  input  Bin,
  output A_XOR_B,
  output BORROW,
  output BORROW_2,
  output DIFFERENCE
);

  wire and_2_out, and_3_out, not_1_out, not_2_out, not_3_out, xor_2_out;

  xor xor_1 (A_XOR_B, A, B);
  not not_1 (not_1_out, A);
  not not_2 (not_2_out, A_2);
  xor xor_2 (xor_2_out, A_2, B_2);
  and and_1 (BORROW, not_1_out, B);
  and and_2 (and_2_out, not_2_out, B_2);
  not not_3 (not_3_out, xor_2_out);
  xor xor_3 (DIFFERENCE, xor_2_out, Bin);
  and and_3 (and_3_out, not_3_out, Bin);
  or or_1 (BORROW_2, and_2_out, and_3_out);

  // Notes on the sheet:
  //   HALF SUBTRACTOR
  //   A
  //   A
  //   A'
  //   B
  //   A' .B
  //   A'
  //   B
  //   A XOR B
  //   Bin
  //   A XOR B
  //   Bin
  //   DIFFERENCE
  //   (A XOR B)'
  //   A'.B
  //   A XOR B XOR Bin
  //   (A XOR B)'.Bin
  //   FULL SUBTRACTOR
  //   (A'.B) + (A XOR B)'.Bin
endmodule
