// Logisim project asynchronous flip flop.circ as structural Verilog: 1 circuit, main circuit main
module main (
  input  in_1,
  input  in_2,
  input  in_3,
  input  in_4,
  input  in_5,
  output out_6,
  output Q0,
  output Q1,
  output out_9,
  output Q2,
  output out_11,
  output Q3,
  output out_13,
  output out_14
);

  wire and_1_out, and_2_out, and_3_out, and_4_out, and_5_out, and_6_out, and_7_out, and_8_out, clock_1_out,
       d_ff_1_qn, d_ff_2_qn, d_ff_3_qn, nor_2_out, nor_4_out, nor_6_out, not_1_out, not_2_out, not_3_out,
       not_4_out;

  not not_1 (not_1_out, in_2);
  not not_2 (not_2_out, nor_2_out);
  not not_3 (not_3_out, nor_4_out);
  not not_4 (not_4_out, nor_6_out);
  and and_1 (and_1_out, not_1_out, in_1);
  and and_2 (and_2_out, in_1, in_2);
  and and_3 (and_3_out, not_2_out, in_3);
  and and_4 (and_4_out, in_3, nor_2_out);
  and and_5 (and_5_out, not_3_out, in_4);
  and and_6 (and_6_out, in_4, nor_4_out);
  and and_7 (and_7_out, not_4_out, in_5);
  and and_8 (and_8_out, in_5, nor_6_out);
  nor nor_1 (out_6, and_1_out, nor_2_out);
  nor nor_2 (nor_2_out, out_6, and_2_out);
  nor nor_3 (out_9, and_3_out, nor_4_out);
  nor nor_4 (nor_4_out, out_9, and_4_out);
  nor nor_5 (out_11, and_5_out, nor_6_out);
  nor nor_6 (nor_6_out, out_11, and_6_out);
  nor nor_7 (out_13, and_7_out, out_14);
  nor nor_8 (out_14, out_13, and_8_out);
  Clock clock_1 (.out(clock_1_out));
  D_Flip_Flop d_ff_1 (.clk(clock_1_out), .D(d_ff_1_qn), .Q(Q0), .Qn(d_ff_1_qn));  // open: preset, en, reset
  D_Flip_Flop d_ff_2 (.clk(d_ff_1_qn), .D(d_ff_2_qn), .Q(Q1), .Qn(d_ff_2_qn));  // open: preset, en, reset
  D_Flip_Flop d_ff_3 (.clk(d_ff_2_qn), .D(d_ff_3_qn), .Q(Q2), .Qn(d_ff_3_qn));  // open: preset, en, reset
  D_Flip_Flop d_ff_4 (.clk(d_ff_3_qn), .Q(Q3));  // open: D, Qn, preset, en, reset

  // Notes on the sheet:
  //   Asynchronous D FlipFlop
endmodule
