// Logisim project jk flip flop to t flip flop.circ as structural Verilog: 1 circuit, main circuit main
module main (
  input  T,
  input  Clk,
  output Q_t,
  output Q_t__prime
);

  wire and_1_out, and_2_out;

  and and_1 (and_1_out, Q_t, T, Clk);
  and and_2 (and_2_out, Clk, T, Q_t__prime);
  nor nor_1 (Q_t, and_1_out, Q_t__prime);
  nor nor_2 (Q_t__prime, Q_t, and_2_out);

  // Notes on the sheet:
  //   JK flip flop TO T flip flop
  //   J
  //   K
endmodule
