// Logisim project jk flipflop to d.circ as structural Verilog: 1 circuit, main circuit main
module main (
  input  D,
  input  Clk,
  output Q_t,
  output Q_t__prime
);

  wire and_1_out, and_2_out, not_1_out;

  not not_1 (not_1_out, D);
  and and_1 (and_1_out, Q_t, D, Clk);
  and and_2 (and_2_out, Clk, not_1_out, Q_t__prime);
  nor nor_1 (Q_t, and_1_out, Q_t__prime);
  nor nor_2 (Q_t__prime, Q_t, and_2_out);

  // Notes on the sheet:
  //   JK flip flop TO D flip flop
  //   J
  //   K
endmodule
