// Logisim project sr to jk flipflop.circ as structural Verilog: 1 circuit, main circuit main
module main (
  input  J,
  input  Clk,
  input  K,
  output Q_t,
  output Q_t__prime
);

  wire and_1_out, and_2_out, and_3_out, and_4_out;

  and and_1 (and_1_out, Q_t, J);
  and and_2 (and_2_out, K, Q_t__prime);
  and and_3 (and_3_out, and_1_out, Clk);
  and and_4 (and_4_out, Clk, and_2_out);
  nor nor_1 (Q_t, and_3_out, Q_t__prime);
  nor nor_2 (Q_t__prime, Q_t, and_4_out);

  // Notes on the sheet:
  //   SR FLIP FLOP TO JK FLIP FLOP
endmodule
