// Logisim project synchronous D flip flop.circ as structural Verilog: 1 circuit, main circuit main
module main (
  input  T,
  output C0,
  output C1,
  output C2,
  output C3
);

  wire and_1_out, and_2_out, clock_1_out, xor_1_out;

  Clock clock_1 (.out(clock_1_out));
  xor xor_1 (xor_1_out, C0, T);
  D_Flip_Flop d_ff_1 (.clk(clock_1_out), .D(xor_1_out), .Q(C0));  // open: Qn, preset, en, reset
  D_Flip_Flop d_ff_2 (.clk(clock_1_out), .Q(C1));  // open: D, Qn, preset, en, reset
  D_Flip_Flop d_ff_3 (.clk(clock_1_out), .D(and_1_out), .Q(C2));  // open: Qn, preset, en, reset
  D_Flip_Flop d_ff_4 (.clk(clock_1_out), .D(and_2_out), .Q(C3));  // open: Qn, preset, en, reset
  and and_1 (and_1_out, C1, C0);
  and and_2 (and_2_out, C2, C1, C0);

  // Notes on the sheet:
  //   Clk
  //   Synchronous D FlipFlop
endmodule
