// Logisim project synchronous flip flops.circ as structural Verilog: 1 circuit, main circuit main
module main (
  input  T,
  output C0,
  output C1,
  output C2,
  output C3
);

  wire and_1_out, and_2_out, clock_1_out;

  Clock clock_1 (.out(clock_1_out));
  T_Flip_Flop t_ff_1 (.clk(clock_1_out), .T(T), .Q(C0));  // open: Qn, preset, reset, en
  T_Flip_Flop t_ff_2 (.clk(clock_1_out), .T(C0), .Q(C1));  // open: Qn, preset, reset, en
  and and_1 (and_1_out, C1, C0);
  T_Flip_Flop t_ff_3 (.clk(clock_1_out), .T(and_1_out), .Q(C1));  // open: Qn, preset, reset, en
  T_Flip_Flop t_ff_4 (.clk(clock_1_out), .T(and_2_out), .Q(C3));  // open: Qn, preset, reset, en
  and and_2 (and_2_out, C0, C1, C1);

  assign C2 = C1;

  // Notes on the sheet:
  //   Clk
  //   Synchoronous T FlipFlop
endmodule
